// Logisim project Group1_Project.circ as structural Verilog: 18 circuits, main circuit HA
module HA (
  input  A,
  input  B,
  output Sum,
  output Carry
);

  and and_1 (Carry, A, B);
  xor xor_1 (Sum, A, B);
endmodule

module FA (
  input  Carry_in,
  input  A,
  input  B,
  output Sum,
  output Carry_out
);

  wire and_1_out, and_2_out, and_3_out, xor_1_out;

  xor xor_1 (xor_1_out, A, B);
  xor xor_2 (Sum, Carry_in, xor_1_out);
  and and_1 (and_1_out, A, B);
  and and_2 (and_2_out, A, Carry_in);
  and and_3 (and_3_out, B, Carry_in);
  or or_1 (Carry_out, and_1_out, and_2_out, and_3_out);
endmodule

module FA_minimization (
  input  Carry_in,
  input  A,
  input  B,
  output Sum,
  output Carry_out
);

  wire and_1_out, ha_1_carry, ha_1_sum;

  HA ha_1 (.A(A), .B(B), .Sum(ha_1_sum), .Carry(ha_1_carry));
  xor xor_1 (Sum, Carry_in, ha_1_sum);
  and and_1 (and_1_out, Carry_in, ha_1_sum);
  or or_1 (Carry_out, and_1_out, ha_1_carry);
endmodule

module FA_with_2HAs (
  input  Carry_in,
  input  A,
  input  B,
  output Sum,
  output Carry_out
);

  wire ha_1_carry, ha_1_sum, ha_2_carry;

  HA ha_1 (.A(A), .B(B), .Sum(ha_1_sum), .Carry(ha_1_carry));
  HA ha_2 (.A(Carry_in), .B(ha_1_sum), .Sum(Sum), .Carry(ha_2_carry));
  or or_1 (Carry_out, ha_2_carry, ha_1_carry);
endmodule

module Adder_Subtractor (
  input  C_in,
  input  B_inv,
  input  A,
  input  B,
  output Sum,
  output Carry_out
);

  wire xor_1_out;

  xor xor_1 (xor_1_out, B_inv, B);
  FA_with_2HAs fa_with_2has_1 (.Carry_in(C_in), .A(A), .B(xor_1_out), .Sum(Sum), .Carry_out(Carry_out));
endmodule

module Add_Sub_MUX (
  input  B_inv,
  input  Carry_in,
  input  A,
  input  B,
  output Result,
  output Carry_out
);

  wire multiplexer_1_out, not_1_out;

  not not_1 (not_1_out, B);
  Multiplexer #(.enable("false")) multiplexer_1 (.in0(B), .in1(not_1_out), .out(multiplexer_1_out), .sel(B_inv));
  FA_with_2HAs fa_with_2has_1 (.Carry_in(Carry_in), .A(A), .B(multiplexer_1_out), .Sum(Result), .Carry_out(Carry_out));
endmodule

module ALU (
  input  [1:0] Operation___S1S0,
  input  B_inv,
  input  Carry_in,
  input  A,
  input  B,
  output S,
  output Carry_out
);

  wire and_1_out, fa_with_2has_1_sum, multiplexer_1_out, not_1_out, or_1_out;

  not not_1 (not_1_out, B);
  Multiplexer #(.enable("false")) multiplexer_1 (.in0(B), .in1(not_1_out), .out(multiplexer_1_out), .sel(B_inv));
  and and_1 (and_1_out, A, B);
  or or_1 (or_1_out, A, B);
  FA_with_2HAs fa_with_2has_1 (
    .Carry_in(Carry_in), .A(A), .B(multiplexer_1_out), .Sum(fa_with_2has_1_sum), .Carry_out(Carry_out));
  Multiplexer #(.select(2), .enable("false")) multiplexer_2 (
    .in0(and_1_out), .in1(or_1_out), .in2(fa_with_2has_1_sum), .out(S), .sel(Operation___S1S0));  // open: in3
endmodule

module _4_Bit_ALU (
  input  B_inv,
  input  [1:0] Op,
  input  C_in,
  input  [3:0] A,
  input  [3:0] B,
  output [3:0] Result,
  output ZF,
  output OF,
  output SF,
  output CF
);

  wire alu_1_carry_out, alu_2_carry_out, alu_3_carry_out;

  ALU alu_1 (
    .Operation___S1S0(Op), .A(A[0]), .B(B[0]), .S(Result[0]), .Carry_out(alu_1_carry_out), .B_inv(B_inv),
    .Carry_in(C_in));
  ALU alu_2 (
    .Operation___S1S0(Op), .A(A[1]), .B(B[1]), .S(Result[1]), .Carry_out(alu_2_carry_out), .B_inv(B_inv),
    .Carry_in(alu_1_carry_out));
  ALU alu_3 (
    .Operation___S1S0(Op), .A(A[2]), .B(B[2]), .S(Result[2]), .Carry_out(alu_3_carry_out), .B_inv(B_inv),
    .Carry_in(alu_2_carry_out));
  ALU alu_4 (
    .Operation___S1S0(Op), .A(A[3]), .B(B[3]), .S(Result[3]), .Carry_out(CF), .B_inv(B_inv),
    .Carry_in(alu_3_carry_out));
  nor nor_1 (ZF, Result[0], Result[1], Result[2], Result[3]);
  xor xor_1 (OF, alu_3_carry_out, CF);

  assign SF = Result[3];
endmodule

module ControlUnit (
  input  [1:0] A,
  output Bin,
  output C,
  output Op1,
  output Op0
);

  wire not_1_out;

  not not_1 (not_1_out, A[1]);
  and and_1 (Bin, A[0], A[1]);
  and and_2 (Op0, not_1_out, A[0]);

  assign C = Bin;
  assign Op1 = A[1];

  // Notes on the sheet:
  //   B
endmodule

module RF_DeMUX (
  input  CLR,
  input  [1:0] S0,
  input  [3:0] Data,
  input  [1:0] in_4,
  input  [1:0] S1,
  input  CLK,
  input  Read0_Write1,
  output [3:0] READ_1,
  output [3:0] READ_2
);

  wire decoder_1_out0, decoder_1_out1, decoder_1_out2, decoder_1_out3, not_1_out;
  wire [3:0] demultiplexer_1_out0, demultiplexer_1_out1, demultiplexer_1_out2, demultiplexer_1_out3, R1_q,
       R2_q, R3_q, RO_q;

  Demultiplexer #(.select(2), .width(4)) demultiplexer_1 (
    .out0(demultiplexer_1_out0), .out1(demultiplexer_1_out1), .out2(demultiplexer_1_out2),
    .out3(demultiplexer_1_out3), .in(Data), .sel(in_4), .en(Read0_Write1));
  Decoder #(.select(2), .enable("false")) decoder_1 (
    .out0(decoder_1_out0), .out1(decoder_1_out1), .out2(decoder_1_out2), .out3(decoder_1_out3), .sel(in_4));
  not not_1 (not_1_out, Read0_Write1);
  Register #(.width(4)) RO (.D(demultiplexer_1_out0), .en(decoder_1_out0), .Q(RO_q), .clk(CLK), .clr(CLR));
  Register #(.width(4)) R1 (.D(demultiplexer_1_out1), .en(decoder_1_out1), .Q(R1_q), .clk(CLK), .clr(CLR));
  Register #(.width(4)) R2 (.D(demultiplexer_1_out2), .en(decoder_1_out2), .Q(R2_q), .clk(CLK), .clr(CLR));
  Register #(.width(4)) R3 (.D(demultiplexer_1_out3), .en(decoder_1_out3), .Q(R3_q), .clk(CLK), .clr(CLR));
  Multiplexer #(.select(2), .width(4)) multiplexer_1 (
    .in0(RO_q), .in1(R1_q), .in2(R2_q), .in3(R3_q), .out(READ_1), .sel(S0), .en(not_1_out));
  Multiplexer #(.select(2), .width(4)) multiplexer_2 (
    .in0(RO_q), .in1(R1_q), .in2(R2_q), .in3(R3_q), .out(READ_2), .sel(S1), .en(not_1_out));
endmodule

module Register_File (
  input  [3:0] Data,
  input  [1:0] R0,
  input  [1:0] WriteAdd,
  input  [1:0] R1,
  input  CLR,
  input  CLK,
  input  RegWr,
  output [3:0] READ_1,
  output [3:0] READ_2
);

  wire and_1_out, and_2_out, and_3_out, and_4_out, and_5_out, decoder_1_out0, decoder_1_out1, decoder_1_out2,
       decoder_1_out3, not_1_out, not_2_out;
  wire [3:0] R1_q, R2_q, R3_q, RO_q;

  Decoder #(.select(2), .enable("false")) decoder_1 (
    .out0(decoder_1_out0), .out1(decoder_1_out1), .out2(decoder_1_out2), .out3(decoder_1_out3), .sel(WriteAdd));
  and and_1 (and_1_out, CLK, not_1_out);
  and and_2 (and_2_out, decoder_1_out0, and_1_out);
  and and_3 (and_3_out, decoder_1_out1, and_1_out);
  and and_4 (and_4_out, decoder_1_out2, and_1_out);
  and and_5 (and_5_out, decoder_1_out3, and_1_out);
  not not_1 (not_1_out, RegWr);
  Register #(.width(4)) RO (.D(Data), .Q(RO_q), .clk(and_2_out), .clr(not_2_out));  // open: en
  Register #(.width(4)) u_R1 (.D(Data), .Q(R1_q), .clk(and_3_out), .clr(not_2_out));  // open: en
  Register #(.width(4)) R2 (.D(Data), .Q(R2_q), .clk(and_4_out), .clr(not_2_out));  // open: en
  Register #(.width(4)) R3 (.D(Data), .Q(R3_q), .clk(and_5_out), .clr(not_2_out));  // open: en
  not not_2 (not_2_out, CLR);
  Multiplexer #(.select(2), .width(4), .enable("false")) multiplexer_1 (
    .in0(RO_q), .in1(R1_q), .in2(R2_q), .in3(R3_q), .out(READ_1), .sel(R0));
  Multiplexer #(.select(2), .width(4), .enable("false")) multiplexer_2 (
    .in0(RO_q), .in1(R1_q), .in2(R2_q), .in3(R3_q), .out(READ_2), .sel(R1));
endmodule

module Data_Memory (
  input  [3:0] Address,
  input  [3:0] WriteData,
  input  MRD,
  input  MWR,
  input  CLK,
  input  CLR,
  output [3:0] ReadData
);

  wire and_1_out, not_1_out, not_2_out, not_3_out, or_1_out;
  wire [3:0] ram_1_data;

  not not_1 (not_1_out, MRD);
  or or_1 (or_1_out, MWR, CLK);
  and and_1 (and_1_out, MWR, not_1_out);
  not not_2 (not_2_out, CLR);
  RAM #(.addrWidth(4), .dataWidth(4)) ram_1 (
    .addr(Address), .data(ram_1_data), .clk(or_1_out), .ld(and_1_out), .clr(not_2_out));  // open: sel
  assign ram_1_data = not_3_out ? WriteData : 4'bz;  // Controlled_Buffer controlled_buffer_1
  not not_3 (not_3_out, and_1_out);
  assign ReadData = and_1_out ? ram_1_data : 4'bz;  // Controlled_Buffer controlled_buffer_2
endmodule

module Instruction_Memory (
  input  [3:0] Address,
  output [15:0] Instruction
);

  ROM #(.addrWidth(4), .dataWidth(16)) rom_1 (.addr(Address), .data(Instruction));  // open: sel
endmodule

module Program_Counter (
  input  CLK,
  input  CLR,
  output [3:0] PC_NEW
);

  wire [3:0] adder_1_out;

  Register #(.width(4)) register_1 (.D(adder_1_out), .Q(PC_NEW), .clk(CLK), .clr(CLR));  // open: en
  Adder #(.width(4)) adder_1 (.a(4'b0001), .b(PC_NEW), .out(adder_1_out));  // open: cin, cout
endmodule

module FINAL_Project (
  input  CLK,
  input  CLR_prime,
  input  RESET,
  input  [1:0] in_4,
  input  in_5
);

  wire BNE_out, controller_1_a_s, controller_1_alusrc, controller_1_br, controller_1_cin, controller_1_j,
       controller_1_memtoreg, controller_1_mrd, controller_1_mwr, controller_1_regdst, controller_1_rwr,
       multiplexer_3_out, n4_bit_alu_1_zf, not_1_out;
  wire [1:0] controller_1_a0, multiplexer_1_out, multiplexer_2_out;
  wire [3:0] data_memory_1_readdata, multiplexer_4_out, multiplexer_5_out, multiplexer_6_out,
       multiplexer_7_out, n4_bit_alu_1_result, n4fa_1_out_3, n4fa_2_out_3, register_1_q,
       register_file_1_read_1, register_file_1_read_2;
  wire [15:0] rom_1_data;

  Register #(.width(4)) register_1 (.D(multiplexer_6_out), .Q(register_1_q), .clk(CLK), .clr(RESET));  // open: en
  _4FA u_4fa_1 (.in_1(4'b0001), .in_2(register_1_q), .out_3(n4fa_1_out_3));
  ROM #(.addrWidth(4), .dataWidth(16)) rom_1 (.addr(register_1_q), .data(rom_1_data));  // open: sel
  Multiplexer #(.width(2), .enable("false")) multiplexer_1 (
    .in0(rom_1_data[5:4]), .in1(rom_1_data[3:2]), .out(multiplexer_1_out), .sel(controller_1_regdst));
  Controller controller_1 (
    .A1(controller_1_a0[1]), .A0(controller_1_a0[0]), .A_S(controller_1_a_s), .Cin(controller_1_cin),
    .RWR(controller_1_rwr), .MRD(controller_1_mrd), .MWR(controller_1_mwr), .ALUsrc(controller_1_alusrc),
    .BR(controller_1_br), .J(controller_1_j), .REGDST(controller_1_regdst), .MemToReg(controller_1_memtoreg),
    .in_1(rom_1_data[11:8]));
  // Probe on rom_1_data[5:4]
  // Probe on multiplexer_1_out
  // Probe on rom_1_data[3:0]
  Multiplexer #(.width(2), .enable("false")) multiplexer_2 (
    .in0(rom_1_data[7:6]), .in1(in_4), .out(multiplexer_2_out), .sel(in_5));
  Multiplexer #(.enable("false")) multiplexer_3 (
    .in0(CLK), .in1(controller_1_rwr), .out(multiplexer_3_out), .sel(rom_1_data[11]));
  Register_File register_file_1 (
    .Data(multiplexer_7_out), .READ_1(register_file_1_read_1), .R0(multiplexer_2_out),
    .READ_2(register_file_1_read_2), .R1(rom_1_data[5:4]), .WriteAdd(multiplexer_1_out), .CLK(CLK),
    .RegWr(multiplexer_3_out), .CLR(CLR_prime));
  _4FA u_4fa_2 (.in_1(n4fa_1_out_3), .in_2(rom_1_data[3:0]), .out_3(n4fa_2_out_3));
  // Probe on register_file_1_read_1
  // Probe on multiplexer_4_out
  Multiplexer #(.width(4), .enable("false")) multiplexer_4 (
    .in0(register_file_1_read_2), .in1(rom_1_data[3:0]), .out(multiplexer_4_out), .sel(controller_1_alusrc));
  Multiplexer #(.width(4), .enable("false")) multiplexer_5 (
    .in0(n4fa_1_out_3), .in1(n4fa_2_out_3), .out(multiplexer_5_out), .sel(BNE_out));
  and BNE (BNE_out, controller_1_br, not_1_out);
  not not_1 (not_1_out, n4_bit_alu_1_zf);
  Multiplexer #(.width(4), .enable("false")) multiplexer_6 (
    .in0(multiplexer_5_out), .in1(rom_1_data[3:0]), .out(multiplexer_6_out), .sel(controller_1_j));
  _4_Bit_ALU u_4_bit_alu_1 (
    .B_inv(controller_1_a_s), .A(register_file_1_read_1), .B(multiplexer_4_out), .Op(controller_1_a0),
    .Result(n4_bit_alu_1_result), .ZF(n4_bit_alu_1_zf), .C_in(controller_1_cin));  // open: OF, SF, CF
  // Probe on multiplexer_7_out
  // Probe on n4_bit_alu_1_result
  // Probe on data_memory_1_readdata
  Data_Memory data_memory_1 (
    .Address(n4_bit_alu_1_result), .WriteData(register_file_1_read_2), .ReadData(data_memory_1_readdata),
    .MRD(controller_1_mrd), .MWR(controller_1_mwr), .CLK(CLK), .CLR(CLR_prime));
  Multiplexer #(.width(4), .enable("false")) multiplexer_7 (
    .in0(n4_bit_alu_1_result), .in1(data_memory_1_readdata), .out(multiplexer_7_out),
    .sel(controller_1_memtoreg));

  // Notes on the sheet:
  //   PC
  //   FA
  //   IR
  //   contents of rom_1 (hex, n*v repeats v):
  //   607 758 ee2 bb3 557 447 c08 218 218 fef
  //   CLR is Active Low
  //   KEEP 1 for circuit
  //   RegD
  //   CONTROLLER
  //   FA
  //   ALUSRC
  //   Br
  //   J
  //   MemToReg
  //   CPU
  //   RISC Based 4-bit Processor
endmodule

module Controller (
  input  [3:0] in_1,
  output A1,
  output A0,
  output A_S,
  output Cin,
  output RWR,
  output MRD,
  output MWR,
  output ALUsrc,
  output BR,
  output J,
  output REGDST,
  output MemToReg
);

  wire and_1_out, and_2_out, and_5_out, and_8_out, and_9_out, and_11_out, not_1_out, not_2_out, not_3_out,
       not_4_out, not_5_out, not_6_out, not_7_out, not_8_out, not_9_out, not_10_out, not_11_out, not_12_out,
       not_13_out, or_2_out, or_3_out, or_4_out;

  and and_1 (and_1_out, in_1[3], in_1[1]);
  not not_1 (not_1_out, in_1[2]);
  not not_2 (not_2_out, in_1[1]);
  not not_3 (not_3_out, in_1[2]);
  not not_4 (not_4_out, in_1[1]);
  not not_5 (not_5_out, in_1[1]);
  not not_6 (not_6_out, in_1[0]);
  or or_1 (A1, in_1[1], in_1[3]);
  or or_2 (or_2_out, in_1[0], in_1[3]);
  not not_7 (not_7_out, in_1[1]);
  not not_8 (not_8_out, in_1[2]);
  not not_9 (not_9_out, in_1[3]);
  or or_3 (or_3_out, not_1_out, in_1[0]);
  not not_10 (not_10_out, in_1[3]);
  not not_11 (not_11_out, in_1[2]);
  and and_2 (and_2_out, in_1[3], not_2_out, in_1[0]);
  and and_3 (BR, in_1[3], not_3_out, in_1[1]);
  and and_4 (J, in_1[3], in_1[2], not_4_out);
  and and_5 (and_5_out, not_5_out, not_6_out);
  or or_4 (or_4_out, and_5_out, not_12_out);
  not not_12 (not_12_out, in_1[3]);
  and and_6 (MemToReg, in_1[3], in_1[1]);
  and and_7 (A0, or_2_out, not_7_out);
  and and_8 (and_8_out, in_1[3], not_8_out);
  and and_9 (and_9_out, not_9_out, in_1[0]);
  and and_10 (RWR, and_1_out, or_3_out);
  or or_5 (MRD, not_10_out, not_11_out, in_1[0]);
  and and_11 (and_11_out, in_1[3], in_1[2], in_1[0]);
  or or_6 (ALUsrc, in_1[2], and_2_out);
  and and_12 (REGDST, or_4_out, not_13_out);
  not not_13 (not_13_out, in_1[2]);
  or or_7 (A_S, and_8_out, and_9_out);
  not not_14 (MWR, and_11_out);

  assign Cin = A_S;
endmodule

module Controller_test (
  input  [3:0] in_1,
  output out_2,
  output out_3,
  output out_4,
  output out_5,
  output out_6,
  output out_7,
  output out_8,
  output out_9,
  output out_10,
  output out_11,
  output out_12,
  output out_13
);

  Controller controller_1 (
    .A1(out_4), .A0(out_5), .A_S(out_6), .Cin(out_7), .RWR(out_8), .MRD(out_9), .MWR(out_10),
    .ALUsrc(out_13), .BR(out_2), .J(out_3), .REGDST(out_11), .MemToReg(out_12), .in_1(in_1));
endmodule

module _4FA (
  input  [3:0] in_1,
  input  [3:0] in_2,
  output [3:0] out_3
);

  wire fa_with_2has_1_carry_out, fa_with_2has_2_carry_out, fa_with_2has_3_carry_out;

  FA_with_2HAs fa_with_2has_1 (
    .Carry_in(1'b0), .A(in_1[0]), .B(in_2[0]), .Sum(out_3[0]), .Carry_out(fa_with_2has_1_carry_out));
  FA_with_2HAs fa_with_2has_2 (
    .Carry_in(fa_with_2has_1_carry_out), .A(in_1[1]), .B(in_2[1]), .Sum(out_3[1]),
    .Carry_out(fa_with_2has_2_carry_out));
  FA_with_2HAs fa_with_2has_3 (
    .Carry_in(fa_with_2has_2_carry_out), .A(in_1[2]), .B(in_2[2]), .Sum(out_3[2]),
    .Carry_out(fa_with_2has_3_carry_out));
  FA_with_2HAs fa_with_2has_4 (
    .Carry_in(fa_with_2has_3_carry_out), .A(in_1[3]), .B(in_2[3]), .Sum(out_3[3]));  // open: Carry_out
endmodule
